// Logisim project alu.circ as structural Verilog: 1 circuit, main circuit ALU
module ALU (
  input  [31:0] A,
  input  [31:0] B,
  input  [3:0] ALU_Op,
  input  [3:0] in_4,
  output [31:0] Out
);

  wire [31:0] adder_1_out, and_1_out, divider_1_out, divider_1_rem, multiplier_1_cout, multiplier_1_out,
       or_1_out, shifter_1_out, shifter_2_out, shifter_3_out, subtractor_1_out, xor_1_out;

  assign B = {{28{1'b0}}, ALU_Op};  // Bit_Extender bit_extender_1
  Adder #(.width(32)) adder_1 (.a(A), .b(B), .out(adder_1_out), .cin(1'b0));  // open: cout
  Subtractor #(.width(32)) subtractor_1 (.a(A), .b(B), .out(subtractor_1_out), .bin(1'b0));  // open: bout
  Multiplier #(.width(32)) multiplier_1 (
    .a(A), .b(B), .out(multiplier_1_out), .cin({32{1'b0}}), .cout(multiplier_1_cout));
  Divider #(.width(32)) divider_1 (.a(A), .b(B), .out(divider_1_out), .upper({32{1'b0}}), .rem(divider_1_rem));
  Shifter #(.width(32), .shift("lr")) shifter_1 (.in(A), .\dist (A[4:0]), .out(shifter_1_out));
  Shifter #(.width(32)) shifter_2 (.in(A), .\dist (B[4:0]), .out(shifter_2_out));
  Shifter #(.width(32), .shift("ar")) shifter_3 (.in(A), .\dist (B[4:0]), .out(shifter_3_out));
  assign and_1_out = A & B & B;  // AND_Gate and_1, 32 bits wide
  assign or_1_out = A | B | B;  // OR_Gate or_1, 32 bits wide
  ExactlyOne xor_1[31:0] (.out(xor_1_out), .in1(A), .in2(B), .in3(B));
  Multiplexer #(.select(4), .width(32)) multiplexer_1 (
    .in0(adder_1_out), .in1(subtractor_1_out), .in2(multiplier_1_out), .in3(multiplier_1_cout),
    .in4(divider_1_out), .in5(divider_1_rem), .in6(shifter_1_out), .in7(shifter_2_out), .in8(shifter_3_out),
    .in9(and_1_out), .in10(or_1_out), .in11(xor_1_out), .in12({32{1'b0}}), .in13({32{1'b0}}),
    .in14({32{1'b0}}), .in15({32{1'b0}}), .out(Out), .sel(in_4));  // open: en

  // Other names for the same wires on the sheet: Op[3:0] = ALU_Op

  // Notes on the sheet:
  //   Inputs
  //   NOTE
  //   Please do not modify/replace/move/change/delete/etc input and output pins
  //   Outputs
endmodule
