// Logisim project cpu.circ as structural Verilog: 4 circuits, main circuit CPU
module CPU (
  input  [31:0] Instruction,
  input  CLK,
  output [31:0] s0,
  output [31:0] s1,
  output [31:0] t0,
  output [31:0] t1,
  output [31:0] a0,
  output [31:0] ra,
  output [31:0] sp,
  output [31:0] PC
);

  wire pc_1_p1;
  wire [31:0] alu_1_out, immgen_1_out_2, incrementer_1_p1, incrementer_1_p2, incrementer_1_p3, main_1_p1,
       main_1_p3, multiplexer_2_out, multiplexer_3_out, regfile_1_p1, regfile_1_p2, rom_1_data;

  // Incrementer incrementer_1: pin names not known; wires that end beside it: incrementer_1_p1, incrementer_1_p2, incrementer_1_p3
  Multiplexer #(.width(32)) multiplexer_1 (
    .in0(incrementer_1_p2), .in1(main_1_p1), .out(incrementer_1_p3));  // open: sel, en
  // PC pc_1: pin names not known; wires that end beside it: pc_1_p1, pc_1_p1, incrementer_1_p1
  ROM #(.addrWidth(24), .dataWidth(32)) rom_1 (.data(rom_1_data));  // open: addr, sel
  // RegFile regfile_1: pin names not known; wires that end beside it: regfile_1_p1, regfile_1_p2, incrementer_1_p1
  ImmGen immgen_1 (.in_1(rom_1_data), .out_2(immgen_1_out_2));
  Multiplexer #(.width(32)) multiplexer_2 (
    .in0(incrementer_1_p1), .in1(regfile_1_p1), .out(multiplexer_2_out));  // open: sel, en
  Multiplexer #(.width(32)) multiplexer_3 (
    .in0(regfile_1_p2), .in1(immgen_1_out_2), .out(multiplexer_3_out));  // open: sel, en
  ALU alu_1 (.A(multiplexer_2_out), .B(multiplexer_3_out), .Out(alu_1_out));  // open: ALU_Op
  // memory_main main_1: pin names not known; wires that end beside it: main_1_p1, regfile_1_p2, main_1_p3
  Multiplexer #(.select(2), .width(32)) multiplexer_4 (
    .in0(incrementer_1_p2), .in1(alu_1_out), .in2(main_1_p3));  // open: in3, out, sel, en

  // Other names for the same wires on the sheet: fetch_addr[31:0] = PC; INST[31:0] = Instruction

  // Notes on the sheet:
  //   NOTE
  //   Please do not modify/replace/move/change/delete/etc input and output pins
  //   These are debug/test outputs from your circuit
endmodule

module Brcomp (
  input  [31:0] IN,
  input  [31:0] A,
  input  [31:0] B,
  input  [31:0] opcode,
  output [31:0] out_5
);

  wire comparator_1_eq, comparator_1_gt, comparator_1_lt;
  wire [31:0] bit_extender_1_out, bit_extender_2_out, bit_extender_3_out, multiplexer_1_out,
       multiplexer_2_out, multiplexer_3_out, not_1_out;

  Comparator #(.width(32)) comparator_1 (
    .a(A), .b(B), .gt(comparator_1_gt), .eq(comparator_1_eq), .lt(comparator_1_lt));
  Bit_Extender #(.in_width(1), .out_width(32)) bit_extender_1 (.out(bit_extender_1_out));  // open: in
  assign bit_extender_2_out = {{31{1'b0}}, comparator_1_lt};  // Bit_Extender bit_extender_2
  assign bit_extender_3_out = {{31{1'b0}}, comparator_1_eq};  // Bit_Extender bit_extender_3
  Multiplexer #(.width(32)) multiplexer_1 (
    .in0(bit_extender_1_out), .in1(bit_extender_2_out), .out(multiplexer_1_out));  // open: sel, en
  Multiplexer #(.width(32)) multiplexer_2 (
    .in0(multiplexer_1_out), .in1(bit_extender_3_out), .out(multiplexer_2_out));  // open: sel, en
  Multiplexer #(.width(32)) multiplexer_3 (
    .in0(multiplexer_2_out), .in1(not_1_out), .out(multiplexer_3_out));  // open: sel, en
  assign not_1_out = ~multiplexer_2_out;  // NOT_Gate not_1, 32 bits wide
  Multiplexer #(.select(2), .width(32)) multiplexer_4 (
    .in0(IN), .in1(IN), .in2(multiplexer_3_out), .in3(IN), .out(out_5), .sel({opcode[6], opcode[2]}));  // open: en
endmodule

module ImmGen (
  input  [31:0] in_1,
  output [31:0] out_2
);

  wire [2:0] rom_1_data;
  wire [31:0] bit_extender_1_out;
  wire [31:12] undriven;
  wire [31:13] undriven_3;
  wire [31:21] undriven_2;

  assign bit_extender_1_out = {{20{1'b0}}, in_1[31:20]};  // Bit_Extender bit_extender_1
  Multiplexer #(.select(3), .width(32)) multiplexer_1 (
    .in2(bit_extender_1_out), .in3({undriven, in_1[31:25], in_1[11:7]}),
    .in4({undriven_3, 1'b0, in_1[11:8], in_1[30:25], in_1[7], in_1[31]}), .in5({{12{1'b0}}, in_1[31:12]}),
    .in6({undriven_2, 1'b0, in_1[30:12], in_1[31]}), .in7({32{1'b0}}), .out(out_2), .sel(rom_1_data));  // open: in0, in1, en
  ROM #(.addrWidth(7), .dataWidth(3)) rom_1 (.addr(in_1[6:0]), .data(rom_1_data));  // open: sel
endmodule

module ALUctrl (
  input  [31:0] in_1,
  output [3:0] out_2
);

  ROM #(.addrWidth(10), .dataWidth(4)) rom_1 (.addr({in_1[31:25], in_1[14:12]}), .data(out_2));  // open: sel
endmodule
